# Fritzing sketch fritzing_file (saved by Fritzing 0.9.4)
breadboards: 1

parts:
  ESP32 = ESP32S-HiLetgo [part_number=ESP32S-HiLetgo]
  BME280 = BME280
  A3141 = A3144 Hall Effect Sensor. [package="UA [THT]"]

nets:
  N1: ESP32.3.3, BME280.VIN, A3141.+Vsupply
  N2: ESP32.GPIO0, A3141.Out
  N3: ESP32.GPIO21, BME280.SDA
  N4: ESP32.GPIO22, BME280.SCL
  GND: ESP32.GND, BME280.GND, A3141.GND

custom parts:
  ESP32S-HiLetgo: HiLetgo ESP-WROOM-32 ESP32 ESP-32S Development Board 2.4GHz Dual-Mode WiFi + Bluetooth Dual Cores Microcontroller The ESP32 integrated with Antenna switches, RF Balun, power amplifiers, low-noise amplifiers, filters, and management modules, and the entire solution occupies the least area of PCB. 2.4 GHz Wi-Fi plus Bluetooth dual-mode chip, with TSMC Ultra-low power consumption 40nm technology,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
  A3144 Hall Effect Sensor.: Allegro A3144 hall effect switch for high temperature operation.
